# Fritzing sketch 7seg-direct (saved by Fritzing 0.9.5d)
breadboards: 1

parts:
  U1 = LuaNode32 / ESP32 [part_number=ESP32S-PIN30]
  7_Segment1 = 7 Segment Display
  R1 = Resistor [tolerance=±5% resistance=220 package=THT]

nets:
  N1: U1.D25, 7_Segment1.Segment_DP
  N2: U1.D14, 7_Segment1.Segment_E
  N3: U1.D12, 7_Segment1.Segment_C
  N4: U1.D13, 7_Segment1.Segment_D
  N5: U1.GND, R1.Pin_1
  N6: U1.D4, 7_Segment1.Segment_A
  N7: U1.D5, 7_Segment1.Segment_B
  N8: U1.D18, 7_Segment1.Segment_F
  N9: U1.D19, 7_Segment1.Segment_G
  N10: 7_Segment1.common_cathode, R1.Pin_0

custom parts:
  LuaNode32 / ESP32: New Image for LuaNode32 DOIT ESP32 DEVKIT V1. Base parts from LuaNode32 / ESP32 ESP32 based LuaNode32 by G.Noorlander DOIT Esp32 DevKit v1 (30 pins long, 11 pins width) by Werner Rothschopf (modified by vanepp Dec 2018)
