# Fritzing sketch Untitled Sketch 2 (saved by Fritzing 0.9.5d)
circuit board: 5.37424cm x 3.85663cm
breadboards: 1

parts:
  Mod1 = seeeduino-xiao
  U1 = MCP2562 CAN Transceiver [part_number=MCP2562 package="DIP8 [THT]"]
  C9 = Ceramic Capacitor [capacitance=100nF package="100 mil [THT, multilayer]"]  # not connected
  C10 = Ceramic Capacitor [capacitance=100nF package="100 mil [THT, multilayer]"]

nets:
  N1: Mod1.D4, U1.connector3
  N2: Mod1.D5, U1.connector0
  N3: Mod1.3V3, U1.connector4, C10.0
  N4: Mod1.GND, U1.connector1, C10.1
  N5: Mod1.5V, U1.connector2

notes:
  SDは上側が挿入口
  1: DAT2 - N/A
  2: CD/DAT3 - 4
  3: CMD - 23(SPI MOSI)
  4: VDD - +3.3V
  5: CLK - 18(SPI SCLK)
  6: VSS - GND
  7: DAT0 - 19(SPI MISO)
  8: DAT1 - N/A
  9: SWB - N/A
  10: SWA - N/A

custom parts:
  seeeduino-xiao: Seeeduino XIAO processor board.
  MCP2562 CAN Transceiver: The MCP2561/2 is a Microchip Technology Inc. second generation high-speed CAN transceiver. It serves as an interface between a CAN protocol controller and the physical two-wire CAN bus. It has a VIO Supply Pin to Interface Directly to CAN Controllers and Microcontrollers with 1.8V to 5.5V I/O.
