# Fritzing sketch ブレッドボードバージョン (saved by Fritzing 0.9.5d)
breadboards: 1

parts:
  U2 = MCP2562 CAN Transceiver [part_number=MCP2562 package="DIP8 [THT]"]
  U3 = LuaNode32 / ESP32 [part_number=ESP32S-PIN30]
  C3 = Ceramic Capacitor [capacitance=100nF package="100 mil [THT, multilayer]"]
  C4 = Ceramic Capacitor [capacitance=100nF package="100 mil [THT, multilayer]"]

nets:
  N1: U2.connector0, U3.D27
  N2: U2.connector1, U2.connector7, U3.GND, C3.0, C4.0
  N3: U2.connector2, U3.Vin, C3.1
  N4: U2.connector3, U3.D26
  N5: U2.connector4, U3.3V3, C4.1

notes:
  SDは上側が挿入口
  1: DAT2 - N/A
  2: CD/DAT3 - 4
  3: CMD - 23(SPI MOSI)
  4: VDD - +3.3V
  5: CLK - 18(SPI SCLK)
  6: VSS - GND
  7: DAT0 - 19(SPI MISO)
  8: DAT1 - N/A
  9: SWB - N/A
  10: SWA - N/A
  DS3231
  SCL : 21
  SDA : 22
  VCC
  GND
  SD
  2:cd - 4
  3:cmd - 23(MOSI)
  5:clk - 18(SCLK)
  7:dat - 19(MISO)
  CAN
  RXD: 26
  TXD: 27
  RTC
  SCL : 21
  SDA : 22

custom parts:
  MCP2562 CAN Transceiver: The MCP2561/2 is a Microchip Technology Inc. second generation high-speed CAN transceiver. It serves as an interface between a CAN protocol controller and the physical two-wire CAN bus. It has a VIO Supply Pin to Interface Directly to CAN Controllers and Microcontrollers with 1.8V to 5.5V I/O.
  LuaNode32 / ESP32: New Image for LuaNode32 DOIT ESP32 DEVKIT V1. Base parts from LuaNode32 / ESP32 ESP32 based LuaNode32 by G.Noorlander DOIT Esp32 DevKit v1 (30 pins long, 11 pins width) by Werner Rothschopf (modified by vanepp Dec 2018)
