# Fritzing sketch ユニバーサル基板バージョン (saved by Fritzing 0.9.5d)
circuit board: 8.46667cm x 5.64444cm
perfboards: 1

parts:
  J2 = Camdenboss CTB0158-4 [part_number=CTB0158-4 package=THT]
  U4 = LuaNode32 / ESP32 [part_number=ESP32S-PIN30]
  U5 = MCP2562 CAN Transceiver [part_number=MCP2562 package="DIP8 [THT]"]
  C7 = Ceramic Capacitor [capacitance=100nF package="100 mil [THT, multilayer]"]
  C8 = Ceramic Capacitor [capacitance=100nF package="100 mil [THT, multilayer]"]
  microSD1 = MicroSD Card Module

nets:
  N1: J2.pin1, U5.connector5
  N2: J2.pin2, U5.connector6
  N3: J2.pin3, U4.Vin, U5.connector2, C8.1
  GND: J2.pin4, U4.GND, U5.connector1, U5.connector7, C7.1, C8.0, microSD1.GND
  N4: U4.D26, U5.connector3
  N5: U4.D27, U5.connector0
  3V3: U4.3V3, U5.connector4, C7.0, microSD1.VCC
  N6: U4.D4, microSD1.CS
  N7: U4.D18, microSD1.SCK
  N8: U4.D19, microSD1.MISO
  N9: U4.D23, microSD1.MOSI

notes:
  SDは上側が挿入口
  1: DAT2 - N/A
  2: CD/DAT3 - 4
  3: CMD - 23(SPI MOSI)
  4: VDD - +3.3V
  5: CLK - 18(SPI SCLK)
  6: VSS - GND
  7: DAT0 - 19(SPI MISO)
  8: DAT1 - N/A
  9: SWB - N/A
  10: SWA - N/A
  SD
  2:cd - 4
  3:cmd - 23(MOSI)
  5:clk - 18(SCLK)
  7:dat - 19(MISO)
  CAN
  RXD: 26
  TXD: 27

custom parts:
  LuaNode32 / ESP32: New Image for LuaNode32 DOIT ESP32 DEVKIT V1. Base parts from LuaNode32 / ESP32 ESP32 based LuaNode32 by G.Noorlander DOIT Esp32 DevKit v1 (30 pins long, 11 pins width) by Werner Rothschopf (modified by vanepp Dec 2018)
  MCP2562 CAN Transceiver: The MCP2561/2 is a Microchip Technology Inc. second generation high-speed CAN transceiver. It serves as an interface between a CAN protocol controller and the physical two-wire CAN bus. It has a VIO Supply Pin to Interface Directly to CAN Controllers and Microcontrollers with 1.8V to 5.5V I/O.
