# Fritzing sketch practice09 (saved by Fritzing 0.9.5d)
breadboards: 1

parts:
  U1 = LuaNode32 / ESP32 [part_number=ESP32S-PIN30]
  PIR1 = PIR sensor
  R1 = Resistor [tolerance=±5% resistance=220 package="2010 [SMD]"]  # not connected
  LED1 = LED - 5mm [color="Red (633nm)" package="5 mm [THT]"]

nets:
  N1: U1.D13, LED1.anode
  GND: U1.GND, PIR1.GND
  VIN: U1.Vin, PIR1.VDD
  N2: U1.D4, PIR1.SIG

custom parts:
  LuaNode32 / ESP32: New Image for LuaNode32 DOIT ESP32 DEVKIT V1. Base parts from LuaNode32 / ESP32 ESP32 based LuaNode32 by G.Noorlander DOIT Esp32 DevKit v1 (30 pins long, 11 pins width) by Werner Rothschopf (modified by vanepp Dec 2018)
