# Fritzing sketch practice12 (saved by Fritzing 0.9.5d)
breadboards: 1

parts:
  U1 = LuaNode32 / ESP32 [part_number=ESP32S-PIN30]
  パーツ1 = Adafruit AHT20 Temperature and Humidity Sensor [part_number="Adafruit #4566"]

nets:
  GND: U1.GND, パーツ1.GND
  3V3: U1.3V3, パーツ1.VCC
  N1: U1.D21, パーツ1.SDA
  N2: U1.D22, パーツ1.SCL

custom parts:
  LuaNode32 / ESP32: New Image for LuaNode32 DOIT ESP32 DEVKIT V1. Base parts from LuaNode32 / ESP32 ESP32 based LuaNode32 by G.Noorlander DOIT Esp32 DevKit v1 (30 pins long, 11 pins width) by Werner Rothschopf (modified by vanepp Dec 2018)
  Adafruit AHT20 Temperature and Humidity Sensor: The AHT20 is a nice but inexpensive temperature and humidity sensor from the same folks that brought us the DHT22. You can take sensor readings as often as you like, and it uses standard I2C so its super easy to use with any Arduino or Linux/Raspberry Pi board. This sensor has a typical accuracy of +- 2% relative humidity, and +-0.3 °C. There is only one I2C address so its not a good option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
