# Fritzing sketch 7seg (saved by Fritzing 0.9.5d)
breadboards: 1

parts:
  U1 = LuaNode32 / ESP32 [part_number=ESP32S-PIN30]
  U2 = 74HC595 [package="DIP16 [THT]"]
  7_Segment1 = 7 Segment Display
  R1 = Resistor [tolerance=±5% resistance=220 package=THT]

nets:
  GND: U1.GND, U2.GND, U2.OE, R1.Pin_1
  3V3: U1.3V3, U2.MR, U2.VCC
  N1: U1.D18, U2.DS
  N2: U1.D19, U2.ST_CP
  N3: U1.D21, U2.SH_CP
  N4: U2.Q1, 7_Segment1.Segment_B
  N5: U2.Q2, 7_Segment1.Segment_C
  N6: U2.Q3, 7_Segment1.Segment_D
  N7: U2.Q4, 7_Segment1.Segment_E
  N8: U2.Q5, 7_Segment1.Segment_F
  N9: U2.Q6, 7_Segment1.Segment_G
  N10: U2.Q7', 7_Segment1.Segment_DP
  N11: U2.Q0, 7_Segment1.Segment_A
  N12: 7_Segment1.common_cathode, R1.Pin_0

custom parts:
  LuaNode32 / ESP32: New Image for LuaNode32 DOIT ESP32 DEVKIT V1. Base parts from LuaNode32 / ESP32 ESP32 based LuaNode32 by G.Noorlander DOIT Esp32 DevKit v1 (30 pins long, 11 pins width) by Werner Rothschopf (modified by vanepp Dec 2018)
