# Fritzing sketch practice13 (saved by Fritzing 0.9.5d)
breadboards: 1

parts:
  U1 = LuaNode32 / ESP32 [part_number=ESP32S-PIN30]
  U2 = TMP36 [package=to-92]
  R1 = Resistor [tolerance=±5% resistance=1k package=THT]
  R2 = Resistor [tolerance=±5% resistance=1k package=THT]
  R3 = Resistor [tolerance=±5% resistance=1k package=THT]

nets:
  GND: U1.D32, U1.GND, U2.GND, R1.Pin_1, R2.Pin_0, R3.Pin_0
  VIN: U1.Vin, U2.VCC
  N1: U2.VOUT, R1.Pin_0
  N2: R2.Pin_1, R3.Pin_1

notes:
  1kΩ
  1kΩ x 2

custom parts:
  LuaNode32 / ESP32: New Image for LuaNode32 DOIT ESP32 DEVKIT V1. Base parts from LuaNode32 / ESP32 ESP32 based LuaNode32 by G.Noorlander DOIT Esp32 DevKit v1 (30 pins long, 11 pins width) by Werner Rothschopf (modified by vanepp Dec 2018)
