# Fritzing sketch radio_control (saved by Fritzing 0.9.5d)
breadboards: 1

parts:
  Mod1 = seeeduino-xiao
  パーツ1 = Motor Driver 1A Dual TB6612FNG
  M2 = DC Motor
  M1 = DC Motor
  Grove1 = Grove OLED 128x96
  LED5 = LED - 5mm [color="Red (633nm)" package="5 mm [THT]"]
  LED6 = LED - 5mm [color="Red (633nm)" package="5 mm [THT]"]
  U1 = LIPO-110mAh [package=lipo-110]

nets:
  N1: Mod1.D0, パーツ1.AIN1
  N2: Mod1.D1, パーツ1.AIN2
  N3: Mod1.D2, パーツ1.BIN2
  N4: Mod1.D3, パーツ1.BIN1
  N5: Mod1.D4, Grove1.SDA
  N6: Mod1.D5, Grove1.SCL
  N7: Mod1.D9, LED5.anode
  N8: Mod1.D10, LED6.anode
  VCC: Mod1.3V3, パーツ1.VCC, Grove1.VCC, U1.+
  GND: Mod1.GND, パーツ1.GND, Grove1.GND, LED5.cathode, LED6.cathode
  N9: Mod1.5V, パーツ1.STBY
  N10: パーツ1.B01, M1.pin_1
  N11: パーツ1.B02, M1.pin_2
  N12: パーツ1.A02, M2.pin_1
  N13: パーツ1.A01, M2.pin_2

custom parts:
  seeeduino-xiao: Seeeduino XIAO processor board.
